# Fritzing sketch PRISMA (saved by Fritzing 0.9.3b)
breadboards: 2

parts:
  元件3 = Arduino Uno (Rev3)
  HEF3 = HEF4094 [package="DIP16 [THT]"]
  R2 = Resistor [tolerance=±5% resistance=150 package=THT]
  U5 = 74HC595 SMD [package="SO16 [SMD]"]
  U6 = 74HC595 SMD [package="SO16 [SMD]"]
  Disp2 = LBT2088AH [part_number=LBT2088AH]
  LED1 = LED - 5mm [color="Red (633nm)" package="5 mm [THT]"]
  J1 = Piezo Speaker

nets:
  N1: 元件3.A1, U5.SH_CP
  N2: 元件3.A2, U5.DS
  N3: 元件3.A3, U6.ST_CP
  N4: 元件3.A4/SDA, U6.SH_CP
  N5: 元件3.A5/SCL, U6.DS
  N6: 元件3.D8, HEF3.11
  N7: 元件3.D9_PWM, HEF3.9
  N8: 元件3.D2, LED1.anode
  N9: 元件3.D3_PWM, J1.pin2
  N10: 元件3.D5_PWM, HEF3.3
  N11: 元件3.D6_PWM, HEF3.5
  N12: 元件3.D7, HEF3.7
  N13: 元件3.3V3, HEF3.1, R2.Pin_0
  5V: 元件3.5V, U6.VCC
  N14: 元件3.GND, HEF3.8
  N15: U5.Q1, Disp2.pin_3
  N16: U5.Q2, Disp2.pin_4
  N17: U5.Q3, Disp2.pin_10
  N18: U5.Q4, Disp2.pin_6
  N19: U5.Q5, Disp2.pin_11
  N20: U5.Q6, Disp2.pin_15
  N21: U5.Q7, Disp2.pin_16
  N22: U5.GND, U5.OE
  N23: U5.Q0, Disp2.pin_13
  N24: U6.Q1, Disp2.pin_14
  N25: U6.Q2, Disp2.pin_8
  N26: U6.Q3, Disp2.pin_12
  N27: U6.Q4, Disp2.pin1
  N28: U6.Q5, Disp2.pin_7
  N29: U6.Q6, Disp2.pin2
  N30: U6.Q7, Disp2.pin_5
  N31: U6.GND, U6.OE
  N32: U6.Q0, Disp2.pin_9

custom parts:
  HEF4094: (Identical part HCF4094) The HEF4094 is an 8-stage serial shift register. It has a storage latch associated with each stage for strobing data from the serial input to parallel buffered 3-state outputs. The parallel outputs may be connected directly to common bus lines. Data is shifted on positive-going clock transitions. The data in each shift register stage is transferred to the storage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
